// Logisim project circuito de soma.circ as structural Verilog: 3 circuits, main circuit main
module main (
  input  in_1,
  input  in_2,
  input  in_3,
  output out_4,
  output out_5
);

  ADD_1 add_1_1 (.S(out_5), .Vai_1(out_4), .A(in_1), .B(in_2), .Vem_1(in_3));
endmodule

module ADD_1 (
  input  A,
  input  B,
  input  Vem_1,
  output S,
  output Vai_1
);

  wire and_1_out, and_2_out, or_1_out, xor_1_out;

  xor xor_1 (xor_1_out, A, B);
  or or_1 (or_1_out, B, Vem_1);
  xor xor_2 (S, xor_1_out, Vem_1);
  and and_1 (and_1_out, or_1_out, A);
  and and_2 (and_2_out, B, Vem_1);
  or or_2 (Vai_1, and_1_out, and_2_out);
endmodule

module ADD_4 (
  output Overflow
);

  wire add_1_1_vai_1, add_1_3_vai_1, add_1_4_vai_1;
  wire [3:0] add_1_4_s, bitadder_1_out, undriven;

  BitAdder bitadder_1 (.out(bitadder_1_out));  // open: in0
  ADD_1 add_1_1 (
    .S(add_1_4_s[2]), .Vai_1(add_1_1_vai_1), .A(bitadder_1_out[2]), .B(undriven[2]), .Vem_1(add_1_3_vai_1));
  ADD_1 add_1_2 (.S(add_1_4_s[3]), .Vai_1(Overflow), .A(bitadder_1_out[3]), .B(undriven[3]), .Vem_1(add_1_1_vai_1));
  ADD_1 add_1_3 (
    .S(add_1_4_s[1]), .Vai_1(add_1_3_vai_1), .A(bitadder_1_out[1]), .B(undriven[1]), .Vem_1(add_1_4_vai_1));
  ADD_1 add_1_4 (.S(add_1_4_s[0]), .Vai_1(add_1_4_vai_1), .A(bitadder_1_out[0]), .B(undriven[0]), .Vem_1(1'b0));
endmodule
